# Fritzing sketch aq-controller (saved by Fritzing 0.9.3b)
breadboards: 1

parts:
  Part1 = Arduino Uno (Rev3) - ICSP
  U1 = mystery part, 4 pins [chip_label=OLED]
  U2 = mystery part, 5 pins [chip_label=Encoder]
  R1 = Temperature Sensor (Thermistor) [thermistor_type=NTC package=THT]
  R2 = Resistor [tolerance=±5% resistance=10k package=THT]
  U3 = mystery part, 6 pins [chip_label="Relay module"]

nets:
  N1: Part1.A0, U2.pin3
  N2: Part1.A1, U2.pin2
  N3: Part1.A2, U2.pin1
  N4: Part1.A3, R1.pin_0, R2.Pin_0
  N5: Part1.A4/SDA, U1.pin1
  N6: Part1.A5/SCL, U1.pin2
  N7: Part1.D8, U3.pin4
  N8: Part1.D9_PWM, U3.pin3
  N9: Part1.D10_PWM/SS, U3.pin2
  N10: Part1.5V, U1.pin3, U2.pin4, R1.pin_1, U3.pin6
  GND: Part1.GND, U1.pin4, U2.pin5, R2.Pin_1, U3.pin1
